# Fritzing sketch wires (saved by Fritzing 0.9.3b)
breadboards: 1

parts:
  LED1 = smd LED [color="Red (633nm)" package="1206 [SMD]"]
  R1 = Resistor [tolerance=±5% resistance=220 package="2010 [SMD]"]
  IC1 = HJR-3FF-S-Z
  Part3 = Arduino Nano (Rev3.0)
  NRF24L4 = NRF24L01

nets:
  N1: LED1.cathode, IC1.pin5
  N2: LED1.anode, R1.Pin_0
  GND: IC1.GND, Part3.GND, NRF24L4.GND
  5V: IC1.5V, Part3.5V
  N3: IC1.SIG, Part3.D8
  N4: Part3.D9, NRF24L4.CE
  N5: Part3.D10, NRF24L4.CSN
  N6: Part3.D11/MOSI, NRF24L4.MOSI
  N7: Part3.D12/MISO, NRF24L4.MISO
  3V3: Part3.3V3, NRF24L4.VCC
  N8: Part3.D13/SCK, NRF24L4.SCK

custom parts:
  HJR-3FF-S-Z: Relay HJR-3FF-S-Z
  NRF24L01: NRF24L01 module
